// Logisim project cs120lab9-30.circ as structural Verilog
module _2_input_MUX (
  input  in_1,
  input  in_2,
  input  in_3,
  input  in_4,
  input  in_5,
  input  in_6,
  input  in_7,
  input  Cin,
  input  A,
  input  B
);

  wire and_1_out, and_2_out, and_3_out, and_4_out, and_5_out, and_6_out, and_7_out, and_8_out, nand_1_out,
       nand_2_out, not_1_out, not_2_out, not_3_out, not_4_out, not_5_out, or_1_out, or_2_out, xor_1_out,
       xor_2_out;

  not not_1 (not_1_out, in_1);
  and and_1 (and_1_out, not_1_out, not_1_out, in_4);
  and and_2 (and_2_out, in_1, in_5);
  LED led_1 (.in(nand_1_out));
  nand nand_1 (nand_1_out, in_6, nand_2_out);
  nand nand_2 (nand_2_out, nand_1_out, in_7);
  or or_1 (or_1_out, and_1_out, and_2_out);
  LED Out (.in(or_1_out));
  xor xor_1 (xor_1_out, A, B);
  not not_2 (not_2_out, in_3);
  LED led_2 (.in(and_3_out));
  and and_3 (and_3_out, not_2_out, not_3_out);
  not not_3 (not_3_out, in_2);
  LED led_3 (.in(and_4_out));
  and and_4 (and_4_out, in_3, not_4_out);
  not not_4 (not_4_out, in_2);
  not not_5 (not_5_out, in_3);
  and and_5 (and_5_out, not_5_out, in_2);
  LED led_4 (.in(and_5_out));
  and and_6 (and_6_out, in_3, in_2);
  LED led_5 (.in(and_6_out));
  and and_7 (and_7_out, A, B);
  and and_8 (and_8_out, Cin, xor_1_out);
  xor xor_2 (xor_2_out, Cin, xor_1_out);
  or or_2 (or_2_out, and_8_out, and_7_out);
  LED Sum (.in(xor_2_out));
  LED Cout (.in(or_2_out));
endmodule
