// Logisim project traffic.circ as structural Verilog: 1 circuit, main circuit main
module main (
  input  in_1,
  input  in_2,
  output out_3,
  output out_4,
  output out_5,
  output out_6,
  output out_7
);

  wire and_1_out, and_2_out, and_3_out, d_ff_1_q, d_ff_2_q, d_ff_3_q, d_ff_4_q, not_1_out, not_2_out,
       not_3_out, not_4_out, not_5_out, or_3_out, or_4_out;

  not not_1 (not_1_out, d_ff_2_q);
  not not_2 (not_2_out, d_ff_1_q);
  not not_3 (not_3_out, d_ff_2_q);
  not not_4 (not_4_out, d_ff_1_q);
  and and_1 (and_1_out, in_1, not_1_out, not_2_out);
  and and_2 (and_2_out, in_1, not_3_out, d_ff_1_q);
  and and_3 (and_3_out, in_1, d_ff_2_q, not_4_out);
  and and_4 (out_5, in_1, d_ff_2_q, d_ff_1_q);
  D_Flip_Flop d_ff_1 (.clk(in_2), .D(d_ff_3_q), .Q(d_ff_1_q));  // open: Qn, preset, en, reset
  D_Flip_Flop d_ff_2 (.clk(in_2), .D(d_ff_4_q), .Q(d_ff_2_q));  // open: Qn, preset, en, reset
  not not_5 (not_5_out, in_2);
  or or_1 (out_3, and_2_out, and_3_out, out_5);
  or or_2 (out_4, and_3_out, out_5);
  or or_3 (or_3_out, and_2_out, and_3_out);
  or or_4 (or_4_out, and_3_out, and_1_out);
  D_Flip_Flop d_ff_3 (.clk(not_5_out), .D(or_4_out), .Q(d_ff_3_q));  // open: Qn, preset, en, reset
  D_Flip_Flop d_ff_4 (.clk(not_5_out), .D(or_3_out), .Q(d_ff_4_q));  // open: Qn, preset, en, reset

  assign out_6 = out_4;
  assign out_7 = out_3;
endmodule
